# Fritzing sketch Arcade Machine (saved by Fritzing 0.9.3b)
breadboards: 2

parts:
  Part1 = PocketBeagle
  R1 = Resistor [tolerance=±5% resistance=1k package=THT]
  R2 = Resistor [tolerance=±5% resistance=1k package=THT]
  R3 = Resistor [tolerance=±5% resistance=1k package=THT]
  R4 = Resistor [tolerance=±5% resistance=1k package=THT]
  BUTTON1 = Arcade Button (blue)
  BUTTON2 = Arcade Button (white)
  BUTTON3 = Arcade Button (red)
  BUTTON4 = Arcade Button (green)
  Part2 = 0.56" 7-segment LED Backpack [part_number=879]
  LED1 = LED - 5mm [color="White (6500K)" package="5 mm [THT]"]
  LED2 = LED - 5mm [color="Red (633nm)" package="5 mm [THT]"]
  LED3 = LED - 5mm [color="Blue (505nm)" package="5 mm [THT]"]
  LED4 = LED - 5mm [color="Green (570nm)" package="5 mm [THT]"]
  R5 = Resistor [tolerance=±5% resistance=1k package=THT]
  R6 = Resistor [tolerance=±5% resistance=1k package=THT]
  J1 = Piezo Speaker

nets:
  N1: Part1.USB1.ID, LED4.anode
  GND: Part1.GND, R4.Pin_1, BUTTON1.no_name_yet#2, BUTTON2.no_name_yet#2, BUTTON3.no_name_yet#2, BUTTON4.no_name_yet, Part2.GND, LED1.cathode, LED2.cathode, LED3.cathode, LED4.cathode, J1.pin1
  N2: Part1.AIN.VREFN, LED3.anode
  N3: Part1.AIN0(1.8V), R3.Pin_1, BUTTON1.no_name_yet#1
  N4: Part1.I2C2.SDA, Part2.SDA, R5.Pin_0
  N5: Part1.I2C2.SCL, Part2.SCL, R6.Pin_0
  N6: Part1.PRU0.7, LED2.anode
  N7: Part1.PRU0.4, R2.Pin_1, BUTTON3.no_name_yet#1
  N8: Part1.PRU0.1, LED1.anode
  N9: Part1.PRU1.10, R1.Pin_1, BUTTON2.no_name_yet#1
  N10: Part1.PWM0A, J1.pin2
  N11: Part1.3.3V, R1.Pin_0, R2.Pin_0, R3.Pin_0, R4.Pin_0, R5.Pin_1, R6.Pin_1

custom parts:
  Arcade Button (blue): Adafruit Arcade Button (blue)
  Arcade Button (white): Adafruit Arcade Button (white)
  Arcade Button (red): Adafruit Arcade Button (red)
  Arcade Button (green): Adafruit Arcade Button (green)
  0.56" 7-segment LED Backpack: This 0.56" 7-segment LED display includes a driver chip for simple control via an I2C interface. The backpack features address-selection jumpers so you can connect up to eight displays on a single I2C bus.
